// Logisim project ORT2Project.circ as structural Verilog: 8 circuits, main circuit COMPUTER
module COMPUTER (
);

  wire BTN_RST_out, CLK, cpu_1_inta, interrupt_interface_8_1_p4, interrupt_interface_8_1_p5,
       interrupt_interface_8_1_p6, interrupt_interface_8_1_p7, interrupt_interface_8_1_p8,
       interrupt_interface_8_1_p9, interrupt_interface_8_1_p10, interrupt_interface_8_1_p11,
       pull_resistor_2_node, pull_resistor_5_node, ram_1_out_8, rst;
  wire [2:0] cpu_1_uext2__0;
  wire [7:0] interrupt_interface_8_1_p1, pull_resistor_3_node, ram_1_out_7;
  wire [15:0] pull_resistor_4_node;

  Button BTN_RST (.out(BTN_RST_out));
  Clock u_CLK (.out(CLK));
  // RisingEdge risingedge_1: pin names not known; wires that end beside it: BTN_RST_out, CLK, rst
  RAM ram_1 (
    .in_1(pull_resistor_4_node), .in_2(CLK), .in_3(pull_resistor_3_node), .in_4(pull_resistor_2_node),
    .in_5(pull_resistor_5_node), .in_6(rst), .out_7(ram_1_out_7), .out_8(ram_1_out_8));
  Pull_Resistor pull_resistor_1 (.node(ram_1_out_7));
  Pull_Resistor pull_resistor_2 (.node(pull_resistor_2_node));
  Pull_Resistor pull_resistor_3 (.node(pull_resistor_3_node));
  Pull_Resistor pull_resistor_4 (.node(pull_resistor_4_node));
  Pull_Resistor pull_resistor_5 (.node(pull_resistor_5_node));
  Pull_Resistor pull_resistor_6 (.node(ram_1_out_8));
  CPU cpu_1 (
    .in_1(rst), .in_2(CLK), .in_3(ram_1_out_8), .in_4(ram_1_out_7), .ABUS(pull_resistor_4_node),
    .DOUTBUS(pull_resistor_3_node), .out_8(pull_resistor_2_node), .out_9(pull_resistor_5_node),
    .inta(cpu_1_inta), .intr7__0(interrupt_interface_8_1_p1), .UEXT2__0(cpu_1_uext2__0));
  // INTERRUPT_INTERFACE_8 interrupt_interface_8_1: pin names not known; wires that end beside it: interrupt_interface_8_1_p1, cpu_1_inta, cpu_1_uext2__0, interrupt_interface_8_1_p4, interrupt_interface_8_1_p5, interrupt_interface_8_1_p6, interrupt_interface_8_1_p7, interrupt_interface_8_1_p8, interrupt_interface_8_1_p9, interrupt_interface_8_1_p10, interrupt_interface_8_1_p11, CLK
  Button BTN_INTR7 (.out(interrupt_interface_8_1_p4));
  Button BTN_INTR6 (.out(interrupt_interface_8_1_p5));
  Button BTN_INTR5 (.out(interrupt_interface_8_1_p6));
  Button BTN_INTR4 (.out(interrupt_interface_8_1_p7));
  Button BTN_INTR3 (.out(interrupt_interface_8_1_p8));
  Button BTN_INTR2 (.out(interrupt_interface_8_1_p9));
  Button BTN_INTR1 (.out(interrupt_interface_8_1_p10));
  Button BTN_INTR0 (.out(interrupt_interface_8_1_p11));
endmodule

module CPU (
  input  in_1,
  input  in_2,
  input  in_3,
  input  [7:0] in_4,
  input  [7:0] intr7__0,
  output [15:0] ABUS,
  output [7:0] DOUTBUS,
  output out_8,
  output out_9,
  output inta,
  output [2:0] UEXT2__0
);

  wire common_1_mdr0;
  wire [3:0] common_1_phaseffbus;
  wire [5:0] pull_resistor_2_node;
  wire [6:0] common_1_addrbus;
  wire [7:0] pull_resistor_5_node;
  wire [13:0] pull_resistor_4_node;
  wire [14:0] pull_resistor_6_node;
  wire [15:0] A, B, INTRADDR, IVTP, PSW;
  wire [16:0] ALU;
  wire [21:0] common_1_instrucbus;

  COMMON common_1 (
    .CLK(in_2), .RST(in_1), .DIN(in_4), .MAR(ABUS), .A(A), .MDR(DOUTBUS), .ALU(ALU), .IVTPPDSP(INTRADDR),
    .PHASEFFBUS(common_1_phaseffbus), .INSTRUCBUS(common_1_instrucbus), .CMEMBUS(pull_resistor_6_node),
    .CFFBUS(pull_resistor_5_node), .CREGBUS(pull_resistor_4_node), .ADDRBUS(common_1_addrbus),
    .CPSW(pull_resistor_2_node), .PSW(PSW), .B(B), .IVTP(IVTP), .MDR0(common_1_mdr0));
  Pull_Resistor pull_resistor_1 (.node(common_1_instrucbus));
  Pull_Resistor pull_resistor_2 (.node(pull_resistor_2_node));
  Pull_Resistor pull_resistor_3 (.node(common_1_phaseffbus));
  Pull_Resistor pull_resistor_4 (.node(pull_resistor_4_node));
  Pull_Resistor pull_resistor_5 (.node(pull_resistor_5_node));
  Pull_Resistor pull_resistor_6 (.node(pull_resistor_6_node));
  Pull_Resistor pull_resistor_7 (.node(common_1_addrbus));
  FETCH fetch_1 (
    .in_1(in_1), .in_2(in_2), .in_3(in_3), .PHASEFFBUS(common_1_phaseffbus),
    .INSTRUCBUS(common_1_instrucbus), .ADDRBUS(common_1_addrbus), .PSW(PSW), .rdMEM(out_9),
    .CMEMBUS(pull_resistor_6_node), .CFFBUS(pull_resistor_5_node), .CREGBUS(pull_resistor_4_node));
  ADDR addr_1 (
    .in_1(in_1), .in_2(in_2), .in_3(in_3), .PHASEFFBUS(common_1_phaseffbus),
    .INSTRUCBUS(common_1_instrucbus), .ADDRBUS(common_1_addrbus), .rdMEM(out_9),
    .CMEMBUS(pull_resistor_6_node), .CFFBUS(pull_resistor_5_node), .CREGBUS(pull_resistor_4_node));
  EXEC exec_1 (
    .in_1(in_1), .in_2(in_2), .in_3(in_3), .B(B), .PHASEFFBUS(common_1_phaseffbus),
    .INSTRUCBUS(common_1_instrucbus), .ADDRBUS(common_1_addrbus), .PSW(PSW), .A(A), .ALU(ALU),
    .CMEMBUS(pull_resistor_6_node), .CFFBUS(pull_resistor_5_node), .CREGBUS(pull_resistor_4_node),
    .CPSW(pull_resistor_2_node), .rdMEM(out_9), .wrMEM(out_8), .MDR0(common_1_mdr0));
  INTR intr_1 (
    .in_1(in_1), .in_2(in_2), .in_3(in_3), .PHASEFFBUS(common_1_phaseffbus),
    .INSTRUCBUS(common_1_instrucbus), .PSW(PSW), .intr(intr7__0), .ADDIVTP(INTRADDR),
    .CMEMBUS(pull_resistor_6_node), .CFFBUS(pull_resistor_5_node), .CREGBUS(pull_resistor_4_node),
    .rdMEM(out_9), .wrMEM(out_8), .UEXT2__0(UEXT2__0), .inta(inta), .IVTP(IVTP));

  // Other names for the same wires on the sheet: CLK = in_2; DIN7__0[7:0] = in_4; FCBUS = in_3; MAR[15:0] = ABUS;
  //   MDR[7:0] = DOUTBUS; RD = out_9; rst = in_1; WR = out_8
endmodule

module COMMON (
  input  CLK,
  input  RST,
  input  [7:0] DIN,
  input  [15:0] A,
  input  [16:0] ALU,
  input  [15:0] IVTPPDSP,
  input  [15:0] IVTP,
  input  [14:0] CMEMBUS,
  input  [7:0] CFFBUS,
  input  [13:0] CREGBUS,
  input  [5:0] CPSW,
  output [15:0] MAR,
  output [7:0] MDR,
  output [3:0] PHASEFFBUS,
  output [21:0] INSTRUCBUS,
  output [6:0] ADDRBUS,
  output [15:0] PSW,
  output [15:0] B,
  output MDR0
);

  wire adr, and_1_out, and_2_out, and_4_out, and_7_out, and_8_out, and_9_out, and_13_out, and_14_out,
       and_15_out, and_16_out, and_17_out, and_18_out, and_21_out, and_22_out, and_23_out, and_24_out,
       and_25_out, and_26_out, and_27_out, and_28_out, and_29_out, and_30_out, and_31_out, and_32_out,
       and_33_out, and_34_out, and_35_out, and_36_out, and_37_out, and_38_out, br, dc3_8_3_p3, dc3_8_3_p4,
       dc3_8_3_p6, jmp_t, mp2_16b_1_p3, nadr, not_1_out, not_5_out, not_6_out, NZ, or_2_out, or_4_out,
       or_5_out, or_6_out, or_7_out, POR, reg16_inc_ld_2_p4, rsff_2_p4, rsff_3_p4, rsff_4_p4, TEN, TEZ, TZ,
       undriven, V, Z;
  wire [7:0] IR7__0, IR15__8, IR23__16, IR31__24, multiplexer_2_out, multiplexer_6_out, multiplexer_7_out;
  wire [15:0] add16_1_p3, GPR15__0, multiplexer_1_out, multiplexer_3_out, multiplexer_4_out, OFS, PC15__0,
       SP15__0;

  Multiplexer #(.select(3), .width(16), .enable("false")) multiplexer_1 (
    .in0(PC15__0), .in1({IR7__0, IR15__8}), .in2(B), .in3(OFS), .in4(SP15__0), .out(multiplexer_1_out),
    .sel(CMEMBUS[9:7]));  // open: in5, in6, in7
  // REG16_INC_LD reg16_inc_ld_1: pin names not known; wires that end beside it: CLK, multiplexer_1_out, MAR, CMEMBUS[0], CMEMBUS[1]
  // REG8_LD reg8_ld_1: pin names not known; wires that end beside it: CLK, MDR, IR31__24, CREGBUS[0]
  // REG8_LD reg8_ld_2: pin names not known; wires that end beside it: CLK, MDR, IR7__0, CREGBUS[3]
  and and_1 (and_1_out, ~IR31__24[7], ~IR31__24[6]);  // AND_Gate
  // DC2_4 dc2_4_1: pin names not known; wires that end beside it: IR31__24[5:4], and_1_out, nadr, br, jmp_t, adr
  and and_2 (and_2_out, ~IR31__24[3], nadr);  // AND_Gate
  // DC3_8 dc3_8_1: pin names not known; wires that end beside it: IR31__24[2:0], and_2_out, INSTRUCBUS[0], INSTRUCBUS[1], INSTRUCBUS[2], INSTRUCBUS[3], INSTRUCBUS[4], INSTRUCBUS[5], INSTRUCBUS[6], INSTRUCBUS[7]
  and and_3 (INSTRUCBUS[8], ~IR31__24[0], ~IR31__24[1], ~IR31__24[2], IR31__24[3], nadr);  // AND_Gate
  and and_4 (and_4_out, ~IR31__24[2], ~IR31__24[3], br);  // AND_Gate
  // DC2_4 dc2_4_2: pin names not known; wires that end beside it: IR31__24[1:0], and_4_out, INSTRUCBUS[9], INSTRUCBUS[10], INSTRUCBUS[11], INSTRUCBUS[12]
  and and_5 (INSTRUCBUS[13], ~IR31__24[0], ~IR31__24[1], IR31__24[2], ~IR31__24[3], br);  // AND_Gate
  and and_6 (INSTRUCBUS[14], ~IR31__24[0], ~IR31__24[1], ~IR31__24[2], ~IR31__24[3], jmp_t);  // AND_Gate
  and and_7 (and_7_out, ~IR31__24[3], adr);  // AND_Gate
  // DC3_8 dc3_8_2: pin names not known; wires that end beside it: IR31__24[3], IR31__24[2], IR31__24[1], IR31__24[0], IR31__24[1:0], IR31__24[2:0], and_7_out, INSTRUCBUS[15], INSTRUCBUS[16], INSTRUCBUS[17], INSTRUCBUS[18], INSTRUCBUS[19], INSTRUCBUS[20], INSTRUCBUS[21]
  // REG16 reg16_1: pin names not known; wires that end beside it: CLK, 16'hf000, SP15__0, RST, CMEMBUS[5], CMEMBUS[6]
  // REG8_LD reg8_ld_3: pin names not known; wires that end beside it: CLK, MDR, IR23__16, CREGBUS[1]
  Multiplexer #(.select(3), .width(8), .enable("false")) multiplexer_2 (
    .in0(DIN), .in1(A[7:0]), .in2(A[15:8]), .in3(PSW[7:0]), .in4(PSW[15:8]), .in5(PC15__0[7:0]),
    .in6(PC15__0[15:8]), .out(multiplexer_2_out), .sel(CMEMBUS[14:12]));  // open: in7
  // REG8_LD reg8_ld_4: pin names not known; wires that end beside it: CLK, multiplexer_2_out, MDR, CMEMBUS[2]
  and and_8 (and_8_out, ~IR23__16[7], adr);  // AND_Gate
  // DC3_8 dc3_8_3: pin names not known; wires that end beside it: IR23__16[6:4], and_8_out, dc3_8_3_p3, dc3_8_3_p4, ADDRBUS[2], dc3_8_3_p6, ADDRBUS[4], ADDRBUS[5], ADDRBUS[6]
  and and_9 (and_9_out, ~IR23__16[0], ~IR23__16[1], ~IR23__16[2], ~IR23__16[3]);  // AND_Gate
  Multiplexer #(.select(2), .width(16), .enable("false")) multiplexer_3 (
    .in0(GPR15__0), .in1(PC15__0), .in2(A), .in3(IVTP), .out(multiplexer_3_out), .sel(CREGBUS[13:12]));
  // REG8_LD reg8_ld_5: pin names not known; wires that end beside it: CLK, MDR, IR15__8, CREGBUS[2]
  and and_10 (ADDRBUS[0], dc3_8_3_p3, and_9_out);
  and and_11 (ADDRBUS[1], dc3_8_3_p4, and_9_out);
  and and_12 (ADDRBUS[3], dc3_8_3_p6, and_9_out);
  // ADD16 add16_1: pin names not known; wires that end beside it: multiplexer_3_out, OFS, add16_1_p3
  Multiplexer #(.select(2), .width(16), .enable("false")) multiplexer_4 (
    .in0({IR15__8, IR23__16}), .in1(B), .in2(OFS), .in3({IR15__8, IR23__16}), .out(multiplexer_4_out),
    .sel(CMEMBUS[11:10]));
  // MP2_16b mp2_16b_1: pin names not known; wires that end beside it: RST, multiplexer_4_out, mp2_16b_1_p3, 16'h1000, 1'b1
  // REG16_INC_LD reg16_inc_ld_2: pin names not known; wires that end beside it: CLK, mp2_16b_1_p3, PC15__0, reg16_inc_ld_2_p4, CMEMBUS[4]
  Multiplexer #(.select(3), .width(16), .enable("false")) multiplexer_5 (
    .in0({16{1'b0}}), .in1(16'h2), .in2(16'hfffe), .in3({{9{IR15__8[7]}}, IR15__8[6:0]}),
    .in4({{9{IR23__16[7]}}, IR23__16[6:0]}), .in5(IVTPPDSP), .out(add16_1_p3), .sel(CREGBUS[11:9]));  // open: in6, in7
  not not_1 (not_1_out, RST);
  // RSFF rsff_1: pin names not known; wires that end beside it: CFFBUS[1], CLK, CFFBUS[0], not_1_out, PHASEFFBUS[0]
  or or_1 (reg16_inc_ld_2_p4, CMEMBUS[3], RST);
  // GPR8x16 gpr8x16_1: pin names not known; wires that end beside it: IR23__16[3:1], CLK, OFS, GPR15__0, CREGBUS[8]
  // RSFF rsff_2: pin names not known; wires that end beside it: CFFBUS[3], CLK, CFFBUS[2], rsff_2_p4, PHASEFFBUS[1]
  not not_2 (rsff_2_p4, RST);
  Multiplexer #(.select(2), .width(8), .enable("false")) multiplexer_6 (
    .in0(IR7__0), .in1(MDR), .in2(GPR15__0[15:8]), .in3({8{1'b0}}), .out(multiplexer_6_out),
    .sel(CREGBUS[7:6]));
  // REG8_LD reg8_ld_6: pin names not known; wires that end beside it: CLK, multiplexer_6_out, B[15:8], CREGBUS[4]
  and and_13 (and_13_out, POR, B[1]);
  and and_14 (and_14_out, Z, NZ);
  and and_15 (and_15_out, POR, B[2]);
  and and_16 (and_16_out, NZ, A[15]);
  and and_17 (and_17_out, POR, B[3]);
  and and_18 (and_18_out, POR, B[4]);
  and and_19 (TEZ, TZ, INSTRUCBUS[18]);
  and and_20 (TEN, INSTRUCBUS[18], ALU[15]);
  and and_21 (and_21_out, undriven, B[15]);
  or or_2 (or_2_out, and_21_out, INSTRUCBUS[7]);
  or or_3 (NZ, INSTRUCBUS[21], INSTRUCBUS[6], INSTRUCBUS[20], INSTRUCBUS[15], INSTRUCBUS[19]);
  // RSFF rsff_3: pin names not known; wires that end beside it: CFFBUS[5], CLK, CFFBUS[4], rsff_3_p4, PHASEFFBUS[2]
  not not_3 (rsff_3_p4, RST);
  and and_22 (and_22_out, POR, B[0]);
  or or_4 (or_4_out, and_13_out, TEZ, and_14_out);
  or or_5 (or_5_out, and_15_out, TEN, and_16_out);
  or or_6 (or_6_out, and_17_out, and_23_out);
  and and_23 (and_23_out, V, INSTRUCBUS[21]);
  or or_7 (or_7_out, and_18_out, and_24_out);
  and and_24 (and_24_out, INSTRUCBUS[21], ALU[16]);
  nor nor_1 (Z, A[0], A[1], A[2], A[3], A[4], A[5], A[6], A[7], A[9], A[10], A[11], A[12], A[13], A[14], A[15], A[8]);
  nor nor_2 (TZ, ALU[0], ALU[1], ALU[2], ALU[3], ALU[4], ALU[5], ALU[6], ALU[7], ALU[9], ALU[10], ALU[11], ALU[12], ALU[13], ALU[14], ALU[15], ALU[8]);
  Multiplexer #(.select(2), .width(8), .enable("false")) multiplexer_7 (
    .in0(IR15__8), .in1(MDR), .in2(GPR15__0[7:0]), .in3(8'h1), .out(multiplexer_7_out), .sel(CREGBUS[7:6]));
  // REG8_LD reg8_ld_7: pin names not known; wires that end beside it: CLK, multiplexer_7_out, B[7:0], CREGBUS[5]
  and and_25 (and_25_out, ~and_22_out, CPSW[0]);  // AND_Gate
  and and_26 (and_26_out, CPSW[0], and_22_out);
  and and_27 (and_27_out, ~or_4_out, CPSW[1]);  // AND_Gate
  and and_28 (and_28_out, CPSW[1], or_4_out);
  and and_29 (and_29_out, ~or_5_out, CPSW[2]);  // AND_Gate
  and and_30 (and_30_out, CPSW[2], or_5_out);
  and and_31 (and_31_out, ~or_6_out, CPSW[3]);  // AND_Gate
  and and_32 (and_32_out, CPSW[3], or_6_out);
  and and_33 (and_33_out, ~or_7_out, CPSW[4]);  // AND_Gate
  and and_34 (and_34_out, CPSW[4], or_7_out);
  and and_35 (and_35_out, ~or_2_out, CPSW[5]);  // AND_Gate
  and and_36 (and_36_out, CPSW[5], or_2_out);
  // RSFF rsff_4: pin names not known; wires that end beside it: CFFBUS[7], CLK, CFFBUS[6], rsff_4_p4, PHASEFFBUS[3]
  not not_4 (rsff_4_p4, RST);
  not not_5 (not_5_out, RST);
  // RSFF rsff_5: pin names not known; wires that end beside it: and_25_out, CLK, and_26_out, not_5_out, PSW[0]
  // RSFF rsff_6: pin names not known; wires that end beside it: and_27_out, CLK, and_28_out, PSW[1]
  // RSFF rsff_7: pin names not known; wires that end beside it: and_29_out, CLK, and_30_out, PSW[2]
  // RSFF rsff_8: pin names not known; wires that end beside it: and_31_out, CLK, and_32_out, PSW[3]
  // RSFF rsff_9: pin names not known; wires that end beside it: and_33_out, CLK, and_34_out, PSW[4]
  not not_6 (not_6_out, RST);
  // RSFF rsff_10: pin names not known; wires that end beside it: and_35_out, CLK, and_36_out, not_6_out, PSW[15]
  and and_37 (and_37_out, A[15], B[15], ~ALU[15]);  // AND_Gate
  and and_38 (and_38_out, ~A[15], ~B[15], ALU[15]);  // AND_Gate
  or or_8 (POR, INSTRUCBUS[2], INSTRUCBUS[4]);
  or or_9 (V, and_37_out, and_38_out);
  nor nor_3 (MDR0, MDR[0], MDR[1], MDR[2], MDR[3], MDR[4], MDR[5], MDR[6], MDR[7]);

  // Other names for the same wires on the sheet: mxMAR0 = CMEMBUS[7]; mxMAR1 = CMEMBUS[8]; mxMAR2 = CMEMBUS[9];
  //   mxMDR0 = CMEMBUS[12]; mxMDR1 = CMEMBUS[13]; mxMDR2 = CMEMBUS[14]; mxOFSS0 = CREGBUS[12]; mxOFSS1 = CREGBUS[13];
  //   mxPC0 = CMEMBUS[10]; mxPC1 = CMEMBUS[11]; mxOFS0 = CREGBUS[9]; mxOFS1 = CREGBUS[10]; mxOFS2 = CREGBUS[11];
  //   mxB0 = CREGBUS[6]; mxB1 = CREGBUS[7]; A15__0[15:0] = A; immed = ADDRBUS[0]; memdir = ADDRBUS[1];
  //   regdir = ADDRBUS[2]; memind = ADDRBUS[3]; preincr = ADDRBUS[4]; postdec = ADDRBUS[5]; regindpom = ADDRBUS[6];
  //   ALU16__0[16:0] = ALU; C = ALU[16]; B7__0[7:0] = B[7:0]; B15__0[15:0] = B; B15__8[7:0] = B[15:8];
  //   stFETCH = CFFBUS[0]; clFETCH = CFFBUS[1]; stADDR = CFFBUS[2]; clADDR = CFFBUS[3]; stEXEC = CFFBUS[4];
  //   clEXEC = CFFBUS[5]; stINTR = CFFBUS[6]; clINTR = CFFBUS[7]; ldMAR = CMEMBUS[0]; incMAR = CMEMBUS[1];
  //   ldMDR = CMEMBUS[2]; ldPC = CMEMBUS[3]; incPC = CMEMBUS[4]; incSP = CMEMBUS[5]; decSP = CMEMBUS[6];
  //   ldPSWSTART = CPSW[0]; ldPSWZ = CPSW[1]; ldPSWN = CPSW[2]; ldPSWV = CPSW[3]; ldPSWC = CPSW[4]; ldPSWI = CPSW[5];
  //   ldIR31__24 = CREGBUS[0]; ldIR23__16 = CREGBUS[1]; ldIR15__8 = CREGBUS[2]; ldIR7__0 = CREGBUS[3];
  //   ldB15__8 = CREGBUS[4]; ldB7__0 = CREGBUS[5]; ldGPR = CREGBUS[8]; Din7__0[7:0] = DIN; HALT = INSTRUCBUS[0];
  //   RTS = INSTRUCBUS[1]; RTI = INSTRUCBUS[2]; PUSHPSW = INSTRUCBUS[3]; POPPSW = INSTRUCBUS[4]; PUSH = INSTRUCBUS[5];
  //   POP = INSTRUCBUS[6]; INTE = INSTRUCBUS[7]; INTD = INSTRUCBUS[8]; BOVF = INSTRUCBUS[9]; BNEQ = INSTRUCBUS[10];
  //   BLEQU = INSTRUCBUS[11]; JLSS = INSTRUCBUS[12]; JLEQ = INSTRUCBUS[13]; JMP = INSTRUCBUS[14]; LD = INSTRUCBUS[15];
  //   ST = INSTRUCBUS[16]; JSR = INSTRUCBUS[17]; TST = INSTRUCBUS[18]; XOR = INSTRUCBUS[19]; STRLEN = INSTRUCBUS[20];
  //   ADD = INSTRUCBUS[21]; IVTPDISP[15:0] = IVTPPDSP; MAR15__0[15:0] = MAR; MDR7__0[7:0] = MDR;
  //   FETCH = PHASEFFBUS[0]; ADDR = PHASEFFBUS[1]; EXEC = PHASEFFBUS[2]; INTR = PHASEFFBUS[3]; PSW15__0[15:0] = PSW;
  //   PSWSTART = PSW[0]; PSWZ = PSW[1]; PSWN = PSW[2]; PSWV = PSW[3]; PSWC = PSW[4]; PSWI = PSW[15]

  // Notes on the sheet:
  //   Stack Pointer
  //   Instrukcijski registar
  //   MAR
  //   Dekoderi za prepoznavanje instrukcije na osnovu sadrzaja registra IR23..16
  //   MDR
  //   SabiracPomeraja
  //   Registarski Fajl
  //   PC
  //   FF za pokretanje FETCH, ADDR, EXEC i INTR faze izvršavanja instrukcije
  //   B
  //   Programska statusna reč (PSW)
endmodule

module FETCH (
  input  in_1,
  input  in_2,
  input  in_3,
  input  [3:0] PHASEFFBUS,
  input  [21:0] INSTRUCBUS,
  input  [6:0] ADDRBUS,
  input  [15:0] PSW,
  output [14:0] CMEMBUS,
  output [7:0] CFFBUS,
  output [13:0] CREGBUS,
  output rdMEM
);

  wire adr, adr2, adr3, and_3_out, and_4_out, br, clFETCH, gradr, grinst, grop, incPC, jmp2, jmp3, ldIR7__0,
       ldIR15__8, ldIR23__16, ldIR31__24, ldMAR, ldMDR, nadr, nand_1_out, nor_2_out, not_1_out, not_3_out,
       or_4_out, or_6_out, or_7_out, rdMEM_t, reg5_cl_inc_ld_1_p7, stADDR, stEXEC;
  wire [3:0] rom_1_data;
  wire [4:0] reg5_cl_inc_ld_1_p4, reg5_cl_inc_ld_1_p5;

  or or_1 (jmp2, INSTRUCBUS[9], INSTRUCBUS[10], INSTRUCBUS[11]);
  or or_2 (jmp3, INSTRUCBUS[12], INSTRUCBUS[13], INSTRUCBUS[14]);
  not not_1 (not_1_out, in_1);
  or or_3 (nadr, INSTRUCBUS[0], INSTRUCBUS[1], INSTRUCBUS[2], INSTRUCBUS[3], INSTRUCBUS[4], INSTRUCBUS[5], INSTRUCBUS[6], INSTRUCBUS[7], INSTRUCBUS[8]);
  // REG5_CL_INC_LD reg5_cl_inc_ld_1: pin names not known; wires that end beside it: 1'b0, in_2, not_1_out, reg5_cl_inc_ld_1_p4, reg5_cl_inc_ld_1_p5, br, reg5_cl_inc_ld_1_p7
  not not_2 (reg5_cl_inc_ld_1_p7, br);
  nand nand_1 (nand_1_out, PHASEFFBUS[0], PSW[0]);
  not not_3 (not_3_out, in_3);
  Multiplexer #(.select(4)) multiplexer_1 (
    .in0(1'b0), .in1(1'b1), .in2(nand_1_out), .in3(not_3_out), .in4(grop), .in5(nadr), .in6(jmp2),
    .in7(gradr), .in8(adr2), .in9(jmp3), .in10(adr3), .out(br), .sel(rom_1_data), .en(1'b1));  // open: in11, in12, in13, in14, in15
  or or_4 (or_4_out, ADDRBUS[2], ADDRBUS[4], ADDRBUS[5]);
  ROM #(.addrWidth(5), .dataWidth(20)) rom_1 (
    .addr(reg5_cl_inc_ld_1_p5),
    .data({reg5_cl_inc_ld_1_p4, rom_1_data, stEXEC, stADDR, clFETCH, ldIR7__0, ldIR15__8, ldIR23__16, ldIR31__24, ldMDR, rdMEM_t, incPC, ldMAR}),
    .sel(1'b1));
  and and_1 (adr2, or_4_out, adr);
  and and_2 (adr3, adr, ADDRBUS[6]);
  or or_5 (adr, INSTRUCBUS[15], INSTRUCBUS[16], INSTRUCBUS[17], INSTRUCBUS[18], INSTRUCBUS[19], INSTRUCBUS[20], INSTRUCBUS[21]);
  or or_6 (or_6_out, ADDRBUS[2], ADDRBUS[0]);
  nor nor_1 (grop, nadr, jmp2, jmp3, adr);
  and and_3 (and_3_out, or_6_out, INSTRUCBUS[20]);
  and and_4 (and_4_out, INSTRUCBUS[16], ADDRBUS[0]);
  nor nor_2 (nor_2_out, ADDRBUS[0], ADDRBUS[1], ADDRBUS[2], ADDRBUS[3], ADDRBUS[4], ADDRBUS[5], ADDRBUS[6]);
  or or_7 (or_7_out, and_3_out, and_4_out, nor_2_out);
  and and_5 (gradr, adr, or_7_out);
  or or_8 (grinst, grop, gradr);
  BUSGATE busgate_1 (.IN(ldMAR), .OUT(CMEMBUS[0]));
  BUSGATE busgate_2 (.IN(ldMDR), .OUT(CMEMBUS[2]));
  BUSGATE busgate_3 (.IN(incPC), .OUT(CMEMBUS[4]));
  BUSGATE busgate_4 (.IN(clFETCH), .OUT(CFFBUS[1]));
  BUSGATE busgate_5 (.IN(stADDR), .OUT(CFFBUS[2]));
  BUSGATE busgate_6 (.IN(stEXEC), .OUT(CFFBUS[4]));
  BUSGATE busgate_7 (.IN(ldIR31__24), .OUT(CREGBUS[0]));
  BUSGATE busgate_8 (.IN(ldIR23__16), .OUT(CREGBUS[1]));
  BUSGATE busgate_9 (.IN(ldIR15__8), .OUT(CREGBUS[2]));
  BUSGATE busgate_10 (.IN(ldIR7__0), .OUT(CREGBUS[3]));
  BUSGATE busgate_11 (.IN(rdMEM_t), .OUT(rdMEM));

  // Other names for the same wires on the sheet: immed = ADDRBUS[0]; memdir = ADDRBUS[1]; regdir = ADDRBUS[2];
  //   memind = ADDRBUS[3]; preincr = ADDRBUS[4]; postdec = ADDRBUS[5]; regindpom = ADDRBUS[6]; CLK = in_2;
  //   FCBUS = in_3; HALT = INSTRUCBUS[0]; RTS = INSTRUCBUS[1]; RTI = INSTRUCBUS[2]; PUSHPSW = INSTRUCBUS[3];
  //   POPPSW = INSTRUCBUS[4]; PUSH = INSTRUCBUS[5]; POP = INSTRUCBUS[6]; INTE = INSTRUCBUS[7]; INTD = INSTRUCBUS[8];
  //   BOVF = INSTRUCBUS[9]; BNEQ = INSTRUCBUS[10]; BLEQU = INSTRUCBUS[11]; JLSS = INSTRUCBUS[12];
  //   JLEQ = INSTRUCBUS[13]; JMP = INSTRUCBUS[14]; LD = INSTRUCBUS[15]; ST = INSTRUCBUS[16]; JSR = INSTRUCBUS[17];
  //   TST = INSTRUCBUS[18]; XOR = INSTRUCBUS[19]; STRLEN = INSTRUCBUS[20]; ADD = INSTRUCBUS[21];
  //   FETCH = PHASEFFBUS[0]; ADDR = PHASEFFBUS[1]; EXEC = PHASEFFBUS[2]; INTR = PHASEFFBUS[3]; PSWST = PSW[0];
  //   rst = in_1

  // Notes on the sheet:
  //   Operaciona jedinica
  //   Kontrolna jedinica
  //   contents of rom_1 (hex, n*v repeats v):
  //   1000 3 1180c 10 2000 9a800 3 3980c 9b020 3800 94000 3 6180c 9c840 95000 3 8180c 80 b00 d00
endmodule

module ADDR (
  input  in_1,
  input  in_2,
  input  in_3,
  input  [3:0] PHASEFFBUS,
  input  [21:0] INSTRUCBUS,
  input  [6:0] ADDRBUS,
  output [14:0] CMEMBUS,
  output [7:0] CFFBUS,
  output [13:0] CREGBUS,
  output rdMEM
);

  wire addrcase, br, clADDR, incMAR, ldB7__0, ldB15__8, ldGPR, ldMAR, ldMDR, mxB0, mxB1, mxMAR0, mxMAR1,
       mxOFS0, mxOFS1, not_1_out, not_3_out, not_4_out, or_1_out, rdMEM_t, reg5_cl_inc_ld_1_p7, stEXEC;
  wire [2:0] rom_1_data;
  wire [4:0] controlled_buffer_1_out, multiplexer_1_out, reg5_cl_inc_ld_1_p5, rom_1_data_2;

  not not_1 (not_1_out, in_1);
  or or_1 (or_1_out, INSTRUCBUS[16], INSTRUCBUS[20]);
  assign controlled_buffer_1_out = ADDRBUS[0] ? 5'b00010 : 5'bz;  // Controlled_Buffer controlled_buffer_1
  assign controlled_buffer_1_out = ADDRBUS[1] ? 5'b00011 : 5'bz;  // Controlled_Buffer controlled_buffer_2
  assign controlled_buffer_1_out = ADDRBUS[2] ? 5'b00100 : 5'bz;  // Controlled_Buffer controlled_buffer_3
  assign controlled_buffer_1_out = ADDRBUS[3] ? 5'b00110 : 5'bz;  // Controlled_Buffer controlled_buffer_4
  Multiplexer #(.width(5), .enable("false")) multiplexer_1 (
    .in0(rom_1_data_2), .in1(controlled_buffer_1_out), .out(multiplexer_1_out), .sel(addrcase));
  // REG5_CL_INC_LD reg5_cl_inc_ld_1: pin names not known; wires that end beside it: 1'b0, in_2, not_1_out, multiplexer_1_out, reg5_cl_inc_ld_1_p5, br, reg5_cl_inc_ld_1_p7
  and and_1 (addrcase, rom_1_data[0], rom_1_data[1], ~rom_1_data[2]);  // AND_Gate
  assign controlled_buffer_1_out = ADDRBUS[4] ? 5'b01100 : 5'bz;  // Controlled_Buffer controlled_buffer_5
  assign controlled_buffer_1_out = ADDRBUS[5] ? 5'b01101 : 5'bz;  // Controlled_Buffer controlled_buffer_6
  assign controlled_buffer_1_out = ADDRBUS[6] ? 5'b01111 : 5'bz;  // Controlled_Buffer controlled_buffer_7
  not not_2 (reg5_cl_inc_ld_1_p7, br);
  not not_3 (not_3_out, PHASEFFBUS[1]);
  not not_4 (not_4_out, in_3);
  ROM #(.addrWidth(5), .dataWidth(23)) rom_1 (
    .addr(reg5_cl_inc_ld_1_p5),
    .data({rom_1_data_2, rom_1_data, stEXEC, clADDR, mxOFS1, ldGPR, mxOFS0, mxMAR1, incMAR, mxB0, ldMDR, rdMEM_t, mxB1, mxMAR0, ldMAR, ldB7__0, ldB15__8}),
    .sel(1'b1));
  Multiplexer #(.select(3), .enable("false")) multiplexer_2 (
    .in0(1'b0), .in1(1'b1), .in2(not_3_out), .in3(1'b1), .in4(INSTRUCBUS[16]), .in5(not_4_out),
    .in6(or_1_out), .out(br), .sel(rom_1_data));  // open: in7
  BUSGATE busgate_1 (.IN(ldMAR), .OUT(CMEMBUS[0]));
  BUSGATE busgate_2 (.IN(incMAR), .OUT(CMEMBUS[1]));
  BUSGATE busgate_3 (.IN(ldMDR), .OUT(CMEMBUS[2]));
  BUSGATE busgate_4 (.IN(mxMAR0), .OUT(CMEMBUS[7]));
  BUSGATE busgate_5 (.IN(mxMAR1), .OUT(CMEMBUS[8]));
  BUSGATE busgate_6 (.IN(ldB15__8), .OUT(CREGBUS[4]));
  BUSGATE busgate_7 (.IN(ldB7__0), .OUT(CREGBUS[5]));
  BUSGATE busgate_8 (.IN(mxB0), .OUT(CREGBUS[6]));
  BUSGATE busgate_9 (.IN(mxB1), .OUT(CREGBUS[7]));
  BUSGATE busgate_10 (.IN(ldGPR), .OUT(CREGBUS[8]));
  BUSGATE busgate_11 (.IN(mxOFS0), .OUT(CREGBUS[9]));
  BUSGATE busgate_12 (.IN(mxOFS1), .OUT(CREGBUS[10]));
  BUSGATE busgate_13 (.IN(clADDR), .OUT(CFFBUS[3]));
  BUSGATE busgate_14 (.IN(stEXEC), .OUT(CFFBUS[4]));
  BUSGATE busgate_15 (.IN(rdMEM_t), .OUT(rdMEM));

  // Other names for the same wires on the sheet: immed = ADDRBUS[0]; memdir = ADDRBUS[1]; regdir = ADDRBUS[2];
  //   memind = ADDRBUS[3]; preincr = ADDRBUS[4]; postdec = ADDRBUS[5]; regindpom = ADDRBUS[6]; CLK = in_2;
  //   FCBUS = in_3; HALT = INSTRUCBUS[0]; RTS = INSTRUCBUS[1]; RTI = INSTRUCBUS[2]; PUSHPSW = INSTRUCBUS[3];
  //   POPPSW = INSTRUCBUS[4]; PUSH = INSTRUCBUS[5]; POP = INSTRUCBUS[6]; INTE = INSTRUCBUS[7]; INTD = INSTRUCBUS[8];
  //   BOVF = INSTRUCBUS[9]; BNEQ = INSTRUCBUS[10]; BLEQU = INSTRUCBUS[11]; JLSS = INSTRUCBUS[12];
  //   JLEQ = INSTRUCBUS[13]; JMP = INSTRUCBUS[14]; LD = INSTRUCBUS[15]; ST = INSTRUCBUS[16]; JSR = INSTRUCBUS[17];
  //   TST = INSTRUCBUS[18]; XOR = INSTRUCBUS[19]; STRLEN = INSTRUCBUS[20]; ADD = INSTRUCBUS[21];
  //   FETCH = PHASEFFBUS[0]; ADDR = PHASEFFBUS[1]; EXEC = PHASEFFBUS[2]; INTR = PHASEFFBUS[3]; rst = in_1

  // Notes on the sheet:
  //   Operaciona jedinica
  //   Upravljacka jedinica
  //   contents of rom_1 (hex, n*v repeats v):
  //   10000 18000 548003 40800c 560000 548013 c 1e8060 182 268060 81 408204 408e0c 20c 409800 40960c
  //   570000 468060 182 4e8060 81 e000
endmodule

module EXEC (
  input  in_1,
  input  in_2,
  input  in_3,
  input  MDR0,
  input  [15:0] B,
  input  [3:0] PHASEFFBUS,
  input  [21:0] INSTRUCBUS,
  input  [6:0] ADDRBUS,
  input  [15:0] PSW,
  output [15:0] A,
  output [16:0] ALU,
  output [14:0] CMEMBUS,
  output [7:0] CFFBUS,
  output [13:0] CREGBUS,
  output [5:0] CPSW,
  output rdMEM,
  output wrMEM
);

  wire aluADD, aluAND, aluXOR, and_3_out, and_4_out, and_5_out, and_6_out, and_7_out, br, CJMP, clA, clEXEC,
       cond, decSP, incMAR, incSP, INTE__INTD, ldA, ldB, ldB7__0, ldB15__8, ldGPR, ldMAR, ldMDR, ldPC,
       ldPSWALL, ldPSWC, ldPSWI, ldPSWN, ldPSWSTART, ldPSWV, ldPSWZ, mp2_16b_1_p3, mxB0, mxB1, mxMAR2,
       mxMDR0, mxMDR1, mxMDR2, mxOFS2, mxOFSS0, mxOFSS1, mxPC0, mxPC1, not_1_out, not_2_out, not_3_out,
       not_4_out, not_6_out, opcase, or_1_out, or_2_out, or_8_out, or_9_out, or_11_out, or_12_out, or_13_out,
       or_14_out, or_15_out, or_16_out, or_17_out, or_18_out, POP__RTI, rdMEM_t, reg6_inc_ld_1_p7,
       reg16_ld_1_p4, RJMP, stINTR, wrMEM_t, xor_2_out;
  wire [1:0] cd4_1_p7;
  wire [3:0] rom_1_data;
  wire [5:0] controlled_buffer_1_out, multiplexer_1_out, reg6_inc_ld_1_p5, rom_1_data_2;
  wire [15:0] adder_1_out, and_2_out, xor_1_out;

  or or_1 (or_1_out, clA, in_1);
  // MP2_16b mp2_16b_1: pin names not known; wires that end beside it: or_1_out, ALU[15:0], mp2_16b_1_p3, {16{1'b0}}, 1'b1
  // REG16_LD reg16_ld_1: pin names not known; wires that end beside it: in_2, mp2_16b_1_p3, A, reg16_ld_1_p4
  or or_2 (or_2_out, INSTRUCBUS[15], INSTRUCBUS[6]);
  not not_1 (not_1_out, cond);
  or or_3 (reg16_ld_1_p4, in_1, clA, ldA);
  not not_2 (not_2_out, in_1);
  and and_1 (opcase, ~rom_1_data[3], ~rom_1_data[2], rom_1_data[1], rom_1_data[0]);  // AND_Gate
  assign controlled_buffer_1_out = INSTRUCBUS[0] ? 6'b000010 : 6'bz;  // Controlled_Buffer controlled_buffer_1
  assign controlled_buffer_1_out = INSTRUCBUS[1] ? 6'b010000 : 6'bz;  // Controlled_Buffer controlled_buffer_2
  assign controlled_buffer_1_out = INSTRUCBUS[3] ? 6'b011110 : 6'bz;  // Controlled_Buffer controlled_buffer_3
  assign controlled_buffer_1_out = INSTRUCBUS[4] ? 6'b001010 : 6'bz;  // Controlled_Buffer controlled_buffer_4
  assign controlled_buffer_1_out = INSTRUCBUS[5] ? 6'b010110 : 6'bz;  // Controlled_Buffer controlled_buffer_5
  assign controlled_buffer_1_out = POP__RTI ? 6'b000011 : 6'bz;  // Controlled_Buffer controlled_buffer_6
  assign controlled_buffer_1_out = INTE__INTD ? 6'b101100 : 6'bz;  // Controlled_Buffer controlled_buffer_7
  assign controlled_buffer_1_out = RJMP ? 6'b101101 : 6'bz;  // Controlled_Buffer controlled_buffer_8
  assign controlled_buffer_1_out = CJMP ? 6'b110111 : 6'bz;  // Controlled_Buffer controlled_buffer_9
  Multiplexer #(.width(6), .enable("false")) multiplexer_1 (
    .in0(rom_1_data_2), .in1(controlled_buffer_1_out), .out(multiplexer_1_out), .sel(opcase));
  // REG6_INC_LD reg6_inc_ld_1: pin names not known; wires that end beside it: 1'b0, in_2, not_2_out, multiplexer_1_out, reg6_inc_ld_1_p5, br, reg6_inc_ld_1_p7
  not not_3 (not_3_out, PHASEFFBUS[2]);
  not not_4 (not_4_out, in_3);
  assign controlled_buffer_1_out = INSTRUCBUS[14] ? 6'b101010 : 6'bz;  // Controlled_Buffer controlled_buffer_10
  assign controlled_buffer_1_out = INSTRUCBUS[15] ? 6'b001000 : 6'bz;  // Controlled_Buffer controlled_buffer_11
  assign controlled_buffer_1_out = INSTRUCBUS[16] ? 6'b011000 : 6'bz;  // Controlled_Buffer controlled_buffer_12
  assign controlled_buffer_1_out = INSTRUCBUS[17] ? 6'b100100 : 6'bz;  // Controlled_Buffer controlled_buffer_13
  assign controlled_buffer_1_out = INSTRUCBUS[18] ? 6'b101111 : 6'bz;  // Controlled_Buffer controlled_buffer_14
  assign controlled_buffer_1_out = INSTRUCBUS[19] ? 6'b110100 : 6'bz;  // Controlled_Buffer controlled_buffer_15
  assign controlled_buffer_1_out = INSTRUCBUS[20] ? 6'b110000 : 6'bz;  // Controlled_Buffer controlled_buffer_16
  assign controlled_buffer_1_out = INSTRUCBUS[21] ? 6'b110101 : 6'bz;  // Controlled_Buffer controlled_buffer_17
  not not_5 (reg6_inc_ld_1_p7, br);
  Multiplexer #(.select(4), .enable("false")) multiplexer_2 (
    .in0(1'b0), .in1(1'b1), .in2(not_3_out), .in3(1'b1), .in4(not_4_out), .in5(or_2_out),
    .in6(INSTRUCBUS[4]), .in7(ADDRBUS[2]), .in8(not_1_out), .in9(MDR0), .in10(cond), .out(br),
    .sel(rom_1_data));  // open: in11, in12, in13, in14, in15
  // CD4 cd4_1: pin names not known; wires that end beside it: aluADD, aluAND, aluXOR, 1'b0, 1'b1, cd4_1_p7[1], cd4_1_p7[0]
  assign xor_1_out = A ^ B;  // XOR_Gate xor_1, 16 bits wide
  assign and_2_out = A & B;  // AND_Gate and_2, 16 bits wide
  Adder #(.width(16)) adder_1 (.a(A), .b(B), .out(adder_1_out), .cout(ALU[16]));  // open: cin
  ROM #(.addrWidth(6), .dataWidth(31)) rom_1 (
    .addr(reg6_inc_ld_1_p5),
    .data({rom_1_data_2, rom_1_data, stINTR, clEXEC, ldPSWV, ldPSWC, aluXOR, aluADD, mxB1, ldB, clA, aluAND, mxOFSS0, mxOFS2, ldPSWI, mxOFSS1, ldGPR, mxPC1, mxMDR2, incMAR, mxMDR1, wrMEM_t, mxMDR0}),
    .sel(1'b1));
  Multiplexer #(.select(2), .width(16), .enable("false")) multiplexer_3 (
    .in0(B), .in1(xor_1_out), .in2(and_2_out), .in3(adder_1_out), .out(ALU[15:0]), .sel(cd4_1_p7));
  ROM #(.addrWidth(6), .dataWidth(16)) rom_2 (
    .addr(reg6_inc_ld_1_p5),
    .data({incSP, mxPC0, ldPC, ldPSWALL, ldPSWN, ldPSWZ, ldA, ldB7__0, mxB0, ldB15__8, ldMDR, rdMEM_t, decSP, mxMAR2, ldMAR, ldPSWSTART}),
    .sel(1'b1));
  or or_4 (POP__RTI, INSTRUCBUS[2], INSTRUCBUS[6]);
  or or_5 (INTE__INTD, INSTRUCBUS[7], INSTRUCBUS[8]);
  or or_6 (CJMP, INSTRUCBUS[12], INSTRUCBUS[13]);
  or or_7 (RJMP, INSTRUCBUS[9], INSTRUCBUS[10], INSTRUCBUS[11]);
  xor xor_2 (xor_2_out, PSW[2], PSW[3]);
  or or_8 (or_8_out, PSW[4], PSW[1]);
  or or_9 (or_9_out, PSW[1], xor_2_out);
  not not_6 (not_6_out, PSW[1]);
  and and_3 (and_3_out, INSTRUCBUS[9], PSW[3]);
  and and_4 (and_4_out, INSTRUCBUS[10], not_6_out);
  and and_5 (and_5_out, INSTRUCBUS[11], or_8_out);
  and and_6 (and_6_out, INSTRUCBUS[12], xor_2_out);
  and and_7 (and_7_out, INSTRUCBUS[13], or_9_out);
  or or_10 (cond, and_3_out, and_4_out, and_5_out, and_6_out, and_7_out);
  or or_11 (or_11_out, ldB15__8, ldB);
  or or_12 (or_12_out, ldB, ldB7__0);
  BUSGATE busgate_1 (.IN(or_11_out), .OUT(CREGBUS[4]));
  BUSGATE busgate_2 (.IN(or_12_out), .OUT(CREGBUS[5]));
  BUSGATE busgate_3 (.IN(mxB0), .OUT(CREGBUS[6]));
  BUSGATE busgate_4 (.IN(mxB1), .OUT(CREGBUS[7]));
  BUSGATE busgate_5 (.IN(ldGPR), .OUT(CREGBUS[8]));
  BUSGATE busgate_6 (.IN(mxOFS2), .OUT(CREGBUS[11]));
  BUSGATE busgate_7 (.IN(mxOFSS0), .OUT(CREGBUS[12]));
  BUSGATE busgate_8 (.IN(mxOFSS1), .OUT(CREGBUS[13]));
  BUSGATE busgate_9 (.IN(ldMAR), .OUT(CMEMBUS[0]));
  BUSGATE busgate_10 (.IN(incMAR), .OUT(CMEMBUS[1]));
  BUSGATE busgate_11 (.IN(ldMDR), .OUT(CMEMBUS[2]));
  BUSGATE busgate_12 (.IN(ldPC), .OUT(CMEMBUS[3]));
  BUSGATE busgate_13 (.IN(incSP), .OUT(CMEMBUS[5]));
  BUSGATE busgate_14 (.IN(decSP), .OUT(CMEMBUS[6]));
  BUSGATE busgate_15 (.IN(mxMAR2), .OUT(CMEMBUS[9]));
  BUSGATE busgate_16 (.IN(mxPC0), .OUT(CMEMBUS[10]));
  BUSGATE busgate_17 (.IN(mxPC1), .OUT(CMEMBUS[11]));
  BUSGATE busgate_18 (.IN(mxMDR0), .OUT(CMEMBUS[12]));
  BUSGATE busgate_19 (.IN(mxMDR1), .OUT(CMEMBUS[13]));
  BUSGATE busgate_20 (.IN(mxMDR2), .OUT(CMEMBUS[14]));
  BUSGATE busgate_21 (.IN(or_13_out), .OUT(CPSW[0]));
  or or_13 (or_13_out, ldPSWALL, ldPSWSTART);
  or or_14 (or_14_out, ldPSWALL, ldPSWZ);
  BUSGATE busgate_22 (.IN(or_14_out), .OUT(CPSW[1]));
  BUSGATE busgate_23 (.IN(or_15_out), .OUT(CPSW[2]));
  or or_15 (or_15_out, ldPSWALL, ldPSWN);
  or or_16 (or_16_out, ldPSWALL, ldPSWV);
  BUSGATE busgate_24 (.IN(or_16_out), .OUT(CPSW[3]));
  or or_17 (or_17_out, ldPSWALL, ldPSWC);
  BUSGATE busgate_25 (.IN(or_17_out), .OUT(CPSW[4]));
  BUSGATE busgate_26 (.IN(or_18_out), .OUT(CPSW[5]));
  or or_18 (or_18_out, ldPSWALL, ldPSWI);
  BUSGATE busgate_27 (.IN(clEXEC), .OUT(CFFBUS[5]));
  BUSGATE busgate_28 (.IN(stINTR), .OUT(CFFBUS[6]));
  BUSGATE busgate_29 (.IN(rdMEM_t), .OUT(rdMEM));
  BUSGATE busgate_30 (.IN(wrMEM_t), .OUT(wrMEM));

  // Other names for the same wires on the sheet: A15__0[15:0] = A; immed = ADDRBUS[0]; memdir = ADDRBUS[1];
  //   regdir = ADDRBUS[2]; memind = ADDRBUS[3]; preincr = ADDRBUS[4]; postdec = ADDRBUS[5]; regindpom = ADDRBUS[6];
  //   ALU16__0[16:0] = ALU; B15__0[15:0] = B; CLK = in_2; FCBUS = in_3; HALT = INSTRUCBUS[0]; RTS = INSTRUCBUS[1];
  //   RTI = INSTRUCBUS[2]; PUSHPSW = INSTRUCBUS[3]; POPPSW = INSTRUCBUS[4]; PUSH = INSTRUCBUS[5]; POP = INSTRUCBUS[6];
  //   INTE = INSTRUCBUS[7]; INTD = INSTRUCBUS[8]; BOVF = INSTRUCBUS[9]; BNEQ = INSTRUCBUS[10]; BLEQU = INSTRUCBUS[11];
  //   JLSS = INSTRUCBUS[12]; JLEQ = INSTRUCBUS[13]; JMP = INSTRUCBUS[14]; LD = INSTRUCBUS[15]; ST = INSTRUCBUS[16];
  //   JSR = INSTRUCBUS[17]; TST = INSTRUCBUS[18]; XOR = INSTRUCBUS[19]; STRLEN = INSTRUCBUS[20]; ADD = INSTRUCBUS[21];
  //   FETCH = PHASEFFBUS[0]; ADDR = PHASEFFBUS[1]; EXEC = PHASEFFBUS[2]; INTR = PHASEFFBUS[3]; PSWSTART = PSW[0];
  //   PSWZ = PSW[1]; PSWN = PSW[2]; PSWV = PSW[3]; PSWC = PSW[4]; PSWI = PSW[15]; rst = in_1

  // Notes on the sheet:
  //   Operaciona jedinica
  //   Upravljacka jedinica
  //   contents of rom_1 (hex, n*v repeats v):
  //   400000 600000 70200000 0 8800000 0 c800000 0 0 70a00000 0 16800000 0 1a800000 0 70c00000 0 22800000
  //   0 26800000 0 70200000 0 0 56e00000 1 34800002 c 38800002 70200000 0 5 40800002 10 44800002 70200000
  //   0 11 4c800002 14 50800002 70200000 70200020 702000c0 70200100 71000000 620 70200800 7000 62800000
  //   6d200000 62208008 6c210000 68000 70200000 55400000 380000
  //   contents of rom_2 (hex, n*v repeats v):
  //   0 0 1 e 30 ce 30 180 200 c00 e 30 ce 30 180 1000 e 30 ce 30 180 6000 8000 8006 0 20 0 20 0 0 8000
  //   8026 0 26 0 0 8000 8026 0 26 0 6000 6000 0 0 0 2000 c00 80 30 0 200 200 200 c00
endmodule

module INTR (
  input  in_1,
  input  in_2,
  input  in_3,
  input  [3:0] PHASEFFBUS,
  input  [21:0] INSTRUCBUS,
  input  [15:0] PSW,
  input  [7:0] intr,
  output [15:0] ADDIVTP,
  output [2:0] UEXT2__0,
  output inta,
  output [15:0] IVTP,
  output [14:0] CMEMBUS,
  output [7:0] CFFBUS,
  output [13:0] CREGBUS,
  output rdMEM,
  output wrMEM
);

  wire br, clINTR, incMAR, incSP, ldB7__0, ldB15__8, ldMAR, ldMDR, ldPC, mxB0, mxMAR0, mxMAR1, mxMAR2,
       mxMDR0, mxMDR1, mxMDR2, mxOFS0, mxOFS2, mxOFSS0, mxOFSS1, mxPC0, not_1_out, not_2_out, not_3_out,
       not_4_out, not_6_out, prekid, priority_encoder_1_gs, rdMEM_t, reg5_cl_inc_ld_1_p7, stFETCH, wrMEM_t;
  wire [2:0] rom_1_data;
  wire [4:0] reg5_cl_inc_ld_1_p4, reg5_cl_inc_ld_1_p5;

  // REG16_LD reg16_ld_1: pin names not known; wires that end beside it: in_2, {16{1'b0}}, IVTP, in_1
  not not_1 (not_1_out, in_1);
  not not_2 (not_2_out, PHASEFFBUS[3]);
  not not_3 (not_3_out, prekid);
  not not_4 (not_4_out, in_3);
  Priority_Encoder priority_encoder_1 (
    .in0(intr[0]), .in1(intr[1]), .in2(intr[2]), .in3(intr[3]), .in4(intr[4]), .in5(intr[5]), .in6(intr[6]),
    .in7(intr[7]), .out(UEXT2__0), .gs(priority_encoder_1_gs));  // open: en_in, en_out
  // REG5_CL_INC_LD reg5_cl_inc_ld_1: pin names not known; wires that end beside it: 1'b0, in_2, not_1_out, reg5_cl_inc_ld_1_p4, reg5_cl_inc_ld_1_p5, br, reg5_cl_inc_ld_1_p7
  not not_5 (reg5_cl_inc_ld_1_p7, br);
  Multiplexer #(.select(3)) multiplexer_1 (
    .in0(1'b0), .in1(1'b1), .in2(not_2_out), .in3(not_3_out), .in4(not_4_out), .out(br), .sel(rom_1_data),
    .en(1'b1));  // open: in5, in6, in7
  and and_1 (prekid, priority_encoder_1_gs, not_6_out, PSW[15]);
  not not_6 (not_6_out, INSTRUCBUS[0]);
  ROM #(.addrWidth(5), .dataWidth(32)) rom_1 (
    .addr(reg5_cl_inc_ld_1_p5),
    .data({reg5_cl_inc_ld_1_p4, rom_1_data, stFETCH, clINTR, mxPC0, ldPC, ldB15__8, incMAR, mxB0, ldB7__0, rdMEM_t, mxOFS2, mxOFS0, mxOFSS1, mxOFSS0, mxMAR1, mxMAR0, mxMDR1, wrMEM_t, mxMDR2, mxMDR0, ldMDR, mxMAR2, ldMAR, incSP, inta}),
    .sel(1'b1));
  // REG3_LD reg3_ld_1: pin names not known; wires that end beside it: in_2, UEXT2__0, ADDIVTP[3:1], inta
  BUSGATE busgate_1 (.IN(ldMAR), .OUT(CMEMBUS[0]));
  BUSGATE busgate_2 (.IN(incMAR), .OUT(CMEMBUS[1]));
  BUSGATE busgate_3 (.IN(ldMDR), .OUT(CMEMBUS[2]));
  BUSGATE busgate_4 (.IN(ldPC), .OUT(CMEMBUS[3]));
  BUSGATE busgate_5 (.IN(incSP), .OUT(CMEMBUS[5]));
  BUSGATE busgate_6 (.IN(mxMAR0), .OUT(CMEMBUS[7]));
  BUSGATE busgate_7 (.IN(mxMAR1), .OUT(CMEMBUS[8]));
  BUSGATE busgate_8 (.IN(mxMAR2), .OUT(CMEMBUS[9]));
  BUSGATE busgate_9 (.IN(mxPC0), .OUT(CMEMBUS[10]));
  BUSGATE busgate_10 (.IN(mxMDR0), .OUT(CMEMBUS[12]));
  BUSGATE busgate_11 (.IN(mxMDR1), .OUT(CMEMBUS[13]));
  BUSGATE busgate_12 (.IN(mxMDR2), .OUT(CMEMBUS[14]));
  BUSGATE busgate_13 (.IN(ldB15__8), .OUT(CREGBUS[4]));
  BUSGATE busgate_14 (.IN(ldB7__0), .OUT(CREGBUS[5]));
  BUSGATE busgate_15 (.IN(mxB0), .OUT(CREGBUS[6]));
  BUSGATE busgate_16 (.IN(mxOFS0), .OUT(CREGBUS[9]));
  BUSGATE busgate_17 (.IN(mxOFS2), .OUT(CREGBUS[11]));
  BUSGATE busgate_18 (.IN(mxOFSS0), .OUT(CREGBUS[12]));
  BUSGATE busgate_19 (.IN(mxOFSS1), .OUT(CREGBUS[13]));
  BUSGATE busgate_20 (.IN(stFETCH), .OUT(CFFBUS[0]));
  BUSGATE busgate_21 (.IN(clINTR), .OUT(CFFBUS[7]));
  BUSGATE busgate_22 (.IN(rdMEM_t), .OUT(rdMEM));
  BUSGATE busgate_23 (.IN(wrMEM_t), .OUT(wrMEM));

  assign {ADDIVTP[15:4], ADDIVTP[0]} = {13{1'b0}};

  // Other names for the same wires on the sheet: ldBRU = inta; ADDIVTP15__0[3:1] = ADDIVTP[3:1]; CLK = in_2;
  //   FCBUS = in_3; HALT = INSTRUCBUS[0]; intr7__0[7:0] = intr; IVTP15__0[15:0] = IVTP; FETCH = PHASEFFBUS[0];
  //   ADDR = PHASEFFBUS[1]; EXEC = PHASEFFBUS[2]; INTR_t = PHASEFFBUS[3]; PSWI = PSW[15]; rst = in_1

  // Notes on the sheet:
  //   Operaciona jedinica
  //   Upravljacka jedinica
  //   contents of rom_1 (hex, n*v repeats v):
  //   2000000 ab000000 3 7e 24000080 15e 34000080 13e 44000080 5e 54000080 3e 64000080 11c 74000080 7e04
  //   84008010 70000 94008010 a0000 300000 1c00000
endmodule

module RAM (
  input  [15:0] in_1,
  input  in_2,
  input  [7:0] in_3,
  input  in_4,
  input  in_5,
  input  in_6,
  output [7:0] out_7,
  output out_8
);

  wire and_1_out, and_2_out, CNT0, LDCNT, not_1_out, notCNT0, or_1_out, reg4_ld_sl_sr_1_p6, rsff_2_p4,
       rsff_2_p5, rsff_3_p4, sl;
  wire [3:0] CNT, LFSR;

  // RSFF rsff_1: pin names not known; wires that end beside it: 1'b0, in_2, in_6, sl
  or or_1 (or_1_out, in_4, in_5);
  // REG4_LD_SL_SR reg4_ld_sl_sr_1: pin names not known; wires that end beside it: 1'b0, 1'b0, in_2, 4'b1111, LFSR, reg4_ld_sl_sr_1_p6, sl, in_6
  // RisingEdge risingedge_1: pin names not known; wires that end beside it: or_1_out, in_2, LDCNT
  // MEM64Kx8 mem64kx8_1: pin names not known; wires that end beside it: in_1, 1'b1, in_2, in_3, out_7, in_4
  xor xor_1 (reg4_ld_sl_sr_1_p6, LFSR[2], LFSR[3]);
  and and_1 (and_1_out, CNT0, not_1_out);
  not not_1 (not_1_out, LDCNT);
  // RSFF rsff_2: pin names not known; wires that end beside it: and_1_out, in_2, LDCNT, rsff_2_p4, rsff_2_p5
  not not_2 (rsff_2_p4, in_6);
  and and_2 (and_2_out, rsff_2_p5, CNT0);
  // REG4m_DEC_LD reg4m_dec_ld_1: pin names not known; wires that end beside it: in_2, LFSR, CNT, LDCNT, notCNT0, notCNT0
  or or_2 (notCNT0, CNT[0], CNT[1], CNT[2], CNT[3]);
  // RSFF rsff_3: pin names not known; wires that end beside it: out_8, in_2, and_2_out, rsff_3_p4, out_8
  not not_3 (rsff_3_p4, in_6);
  not not_4 (CNT0, notCNT0);

  // Other names for the same wires on the sheet: ADR[15:0] = in_1; CLK = in_2; DIN[7:0] = in_3; DOUT[7:0] = out_7;
  //   fc = out_8; RDMEM = in_5; rst = in_6; WRMEM = in_4

  // Notes on the sheet:
  //   Random broj predstavlja vreme pristupa memoriji
  //   Brojac za generisanje random broja 
  //   Jedinica za generisanje function complete (fc) signala
  //   Brojac za dekrementiranje random broja
endmodule
